// Logisim project 010Sequence2022_4.circ as structural Verilog: 1 circuit, main circuit main
module main (
  input  x
);

  wire and_1_out, clock_1_out, j_k_ff_2_q, not_1_out, xor_1_out;

  xor xor_1 (xor_1_out, x, j_k_ff_2_q);
  and and_1 (and_1_out, x, j_k_ff_2_q);
  not not_1 (not_1_out, x);
  Clock clock_1 (.out(clock_1_out));
  J_K_Flip_Flop j_k_ff_1 (.J(and_1_out), .K(xor_1_out), .clk(clock_1_out));  // open: Q, Qn, preset, reset
  J_K_Flip_Flop j_k_ff_2 (.J(not_1_out), .K(x), .clk(clock_1_out), .Q(j_k_ff_2_q));  // open: Qn, preset, reset
endmodule
