// Logisim project 101SequenceJKFF.circ as structural Verilog: 1 circuit, main circuit main
module main (
  input  X,
  output Z
);

  wire and_1_out, button_1_out, button_2_out, button_3_out, clock_1_out, j_k_ff_1_q, j_k_ff_2_q, not_1_out,
       not_2_out, or_1_out;

  not not_1 (not_1_out, X);
  and and_1 (and_1_out, not_1_out, j_k_ff_2_q);
  or or_1 (or_1_out, not_1_out, j_k_ff_2_q);
  Clock clock_1 (.out(clock_1_out));
  J_K_Flip_Flop j_k_ff_1 (
    .J(and_1_out), .K(or_1_out), .clk(clock_1_out), .Q(j_k_ff_1_q), .preset(button_2_out),
    .reset(button_1_out));  // open: Qn
  Button button_1 (.out(button_1_out));
  Button button_2 (.out(button_2_out));
  J_K_Flip_Flop j_k_ff_2 (
    .J(X), .K(not_2_out), .clk(clock_1_out), .Q(j_k_ff_2_q), .preset(button_3_out), .reset(button_1_out));  // open: Qn
  not not_2 (not_2_out, X);
  Button button_3 (.out(button_3_out));
  and and_2 (Z, j_k_ff_2_q, j_k_ff_1_q);
endmodule
