// Logisim project 4x1MUXs_FullAdder.circ as structural Verilog: 1 circuit, main circuit main
module main (
  input  Cin,
  input  [1:0] A_AND_B,
  output S,
  output Cout
);

  wire not_1_out;

  not not_1 (not_1_out, Cin);
  Multiplexer #(.select(2)) multiplexer_1 (
    .in0(Cin), .in1(not_1_out), .in2(not_1_out), .in3(Cin), .out(S), .sel(A_AND_B));
  Multiplexer #(.select(2)) multiplexer_2 (.in0(1'b0), .in1(Cin), .in2(Cin), .in3(1'b1), .out(Cout), .sel(A_AND_B));
endmodule
