// Logisim project DtoT_FF.circ as structural Verilog: 1 circuit, main circuit main
module main (
  input  D
);

  wire Clk_out, t_ff_1_q, xor_1_out;

  xor xor_1 (xor_1_out, t_ff_1_q, D);
  Clock Clk (.out(Clk_out));
  T_Flip_Flop t_ff_1 (.T(xor_1_out), .clk(Clk_out), .Q(t_ff_1_q));  // open: Qn, reset, preset
endmodule
