// Logisim project RS_clocked_FF.circ as structural Verilog: 1 circuit, main circuit main
module main (
  input  R,
  input  Clock,
  input  S,
  output Q,
  output NOT_Q
);

  wire and_1_out, and_2_out;

  and and_1 (and_1_out, R, Clock);
  and and_2 (and_2_out, Clock, S);
  nor nor_1 (Q, and_1_out, NOT_Q);
  nor nor_2 (NOT_Q, Q, and_2_out);
endmodule
