// Logisim project exercise2.circ as structural Verilog: 1 circuit, main circuit main
module main (
  input  X,
  input  Y,
  input  Z,
  output F
);

  wire and_1_out, and_2_out, and_3_out;

  and and_1 (and_1_out, X, Y);
  and and_2 (and_2_out, X, Z);
  or or_1 (F, and_1_out, and_2_out, and_3_out);
  and and_3 (and_3_out, Y, Z);

  // Notes on the sheet:
  //   F = XY + XZ + YZ
endmodule
