// Logisim project FullAdder32bit.circ as structural Verilog
module HalfAdder1bit (
  input  A,
  input  B,
  output S,
  output Cout
);

  xor xor_1 (S, A, B);
  and and_1 (Cout, A, B);
endmodule

module FullAdder1bit (
  input  A,
  input  B,
  input  Cin,
  output S,
  output Cout
);

  wire halfadder1bit_1_cout, halfadder1bit_1_s, halfadder1bit_2_cout;

  HalfAdder1bit halfadder1bit_1 (.A(A), .B(B), .S(halfadder1bit_1_s), .Cout(halfadder1bit_1_cout));
  HalfAdder1bit halfadder1bit_2 (.A(halfadder1bit_1_s), .B(Cin), .S(S), .Cout(halfadder1bit_2_cout));
  or or_1 (Cout, halfadder1bit_2_cout, halfadder1bit_1_cout);
endmodule

module FullAdder4bit (
  input  Cin,
  input  [3:0] A,
  input  [3:0] B,
  output [3:0] S,
  output Cout
);

  wire fulladder1bit_1_cout, fulladder1bit_2_cout, fulladder1bit_3_cout;

  FullAdder1bit fulladder1bit_1 (.A(A[0]), .B(B[0]), .Cin(Cin), .S(S[0]), .Cout(fulladder1bit_1_cout));
  FullAdder1bit fulladder1bit_2 (.A(A[1]), .B(B[1]), .Cin(fulladder1bit_1_cout), .S(S[1]), .Cout(fulladder1bit_2_cout));
  FullAdder1bit fulladder1bit_3 (.A(A[2]), .B(B[2]), .Cin(fulladder1bit_2_cout), .S(S[2]), .Cout(fulladder1bit_3_cout));
  FullAdder1bit fulladder1bit_4 (.A(A[3]), .B(B[3]), .Cin(fulladder1bit_3_cout), .S(S[3]), .Cout(Cout));

  // Notes on the sheet:
  //   C1
  //   C2
endmodule

module FullAdder16bit (
  input  Cin,
  input  [15:0] A,
  input  [15:0] B,
  output [15:0] S,
  output Cout
);

  wire fulladder4bit_1_cout, fulladder4bit_2_cout, fulladder4bit_3_cout;

  FullAdder4bit fulladder4bit_1 (.Cin(Cin), .A(A[3:0]), .B(B[3:0]), .S(S[3:0]), .Cout(fulladder4bit_1_cout));
  FullAdder4bit fulladder4bit_2 (
    .Cin(fulladder4bit_1_cout), .A(A[7:4]), .B(B[7:4]), .S(S[7:4]), .Cout(fulladder4bit_2_cout));
  FullAdder4bit fulladder4bit_3 (
    .Cin(fulladder4bit_2_cout), .A(A[11:8]), .B(B[11:8]), .S(S[11:8]), .Cout(fulladder4bit_3_cout));
  FullAdder4bit fulladder4bit_4 (.Cin(fulladder4bit_3_cout), .A(A[15:12]), .B(B[15:12]), .S(S[15:12]), .Cout(Cout));
  Hex_Digit_Display hex_digit_display_1 (.value(S[11:8]));  // open: dp
  Hex_Digit_Display hex_digit_display_2 (.value(S[15:12]));  // open: dp
  Hex_Digit_Display hex_digit_display_3 (.value(S[7:4]));  // open: dp
  Hex_Digit_Display hex_digit_display_4 (.value(S[3:0]));  // open: dp
endmodule

module FullAdder32bit (
  input  in_1,
  input  [31:0] in_2,
  input  [31:0] in_3,
  output [31:0] out_4,
  output out_5
);

  wire fulladder16bit_1_cout;

  FullAdder16bit fulladder16bit_1 (
    .Cin(in_1), .A(in_2[15:0]), .B(in_3[15:0]), .S(out_4[15:0]), .Cout(fulladder16bit_1_cout));
  FullAdder16bit fulladder16bit_2 (
    .Cin(fulladder16bit_1_cout), .A(in_2[31:16]), .B(in_3[31:16]), .S(out_4[31:16]), .Cout(out_5));
  Hex_Digit_Display hex_digit_display_1 (.value(out_4[31:28]));  // open: dp
  Hex_Digit_Display hex_digit_display_2 (.value(out_4[27:24]));  // open: dp
  Hex_Digit_Display hex_digit_display_3 (.value(out_4[23:20]));  // open: dp
  Hex_Digit_Display hex_digit_display_4 (.value(out_4[19:16]));  // open: dp
  Hex_Digit_Display hex_digit_display_5 (.value(out_4[15:12]));  // open: dp
  Hex_Digit_Display hex_digit_display_6 (.value(out_4[11:8]));  // open: dp
  Hex_Digit_Display hex_digit_display_7 (.value(out_4[7:4]));  // open: dp
  Hex_Digit_Display hex_digit_display_8 (.value(out_4[3:0]));  // open: dp
endmodule
