// Logisim project Comparator4bit.circ as structural Verilog
module Comparator_1bit (
  input  A,
  input  B,
  output A_Greater_B,
  output A_Equal_B,
  output A_Less_B
);

  wire not_1_out, not_2_out;

  not not_1 (not_1_out, B);
  not not_2 (not_2_out, A);
  and and_1 (A_Greater_B, A, not_1_out);
  xnor xnor_1 (A_Equal_B, A, B);
  and and_2 (A_Less_B, not_2_out, B);
endmodule

module Comparator_4bit (
  input  A3,
  input  B3,
  input  A2,
  input  B2,
  input  A1,
  input  B1,
  input  A0,
  input  B0,
  output A_Bigger_B,
  output A_Equal_B,
  output A_Less_B
);

  wire and_1_out, and_2_out, comparator_2bit_1_a_equal_b, comparator_2bit_1_a_greater_b,
       comparator_2bit_1_a_less_b, comparator_2bit_2_a_equal_b, comparator_2bit_2_a_greater_b,
       comparator_2bit_2_a_less_b;

  Comparator_2bit comparator_2bit_1 (
    .A1(A3), .B1(B3), .A0(A2), .B0(B2), .A_Greater_B(comparator_2bit_1_a_greater_b),
    .A_Equal_B(comparator_2bit_1_a_equal_b), .A_Less_B(comparator_2bit_1_a_less_b));
  Comparator_2bit comparator_2bit_2 (
    .A1(A1), .B1(B1), .A0(A0), .B0(B0), .A_Greater_B(comparator_2bit_2_a_greater_b),
    .A_Equal_B(comparator_2bit_2_a_equal_b), .A_Less_B(comparator_2bit_2_a_less_b));
  and and_1 (and_1_out, comparator_2bit_1_a_equal_b, comparator_2bit_2_a_greater_b);
  and and_2 (and_2_out, comparator_2bit_1_a_equal_b, comparator_2bit_2_a_less_b);
  or or_1 (A_Bigger_B, comparator_2bit_1_a_greater_b, and_1_out);
  and and_3 (A_Equal_B, comparator_2bit_1_a_equal_b, comparator_2bit_2_a_equal_b);
  or or_2 (A_Less_B, and_2_out, comparator_2bit_1_a_less_b);
endmodule

module Comparator_2bit (
  input  A1,
  input  B1,
  input  A0,
  input  B0,
  output A_Greater_B,
  output A_Equal_B,
  output A_Less_B
);

  wire and_1_out, and_2_out, comparator_1bit_1_a_equal_b, comparator_1bit_1_a_greater_b,
       comparator_1bit_1_a_less_b, comparator_1bit_2_a_equal_b, comparator_1bit_2_a_greater_b,
       comparator_1bit_2_a_less_b;

  Comparator_1bit comparator_1bit_1 (
    .A(A1), .B(B1), .A_Greater_B(comparator_1bit_1_a_greater_b), .A_Equal_B(comparator_1bit_1_a_equal_b),
    .A_Less_B(comparator_1bit_1_a_less_b));
  Comparator_1bit comparator_1bit_2 (
    .A(A0), .B(B0), .A_Greater_B(comparator_1bit_2_a_greater_b), .A_Equal_B(comparator_1bit_2_a_equal_b),
    .A_Less_B(comparator_1bit_2_a_less_b));
  and and_1 (and_1_out, comparator_1bit_1_a_equal_b, comparator_1bit_2_a_greater_b);
  and and_2 (and_2_out, comparator_1bit_1_a_equal_b, comparator_1bit_2_a_less_b);
  or or_1 (A_Greater_B, comparator_1bit_1_a_greater_b, and_1_out);
  and and_3 (A_Equal_B, comparator_1bit_1_a_equal_b, comparator_1bit_2_a_equal_b);
  or or_2 (A_Less_B, and_2_out, comparator_1bit_1_a_less_b);
endmodule
