// Logisim project Mux8bit2to1.circ as structural Verilog
module mux_2to1_8bit_E (
  input  S,
  input  E,
  input  A0,
  input  B0,
  input  A1,
  input  B1,
  input  A2,
  input  B2,
  input  A3,
  input  B3,
  input  A4,
  input  B4,
  input  A5,
  input  B5,
  input  A6,
  input  B6,
  input  A7,
  input  B7,
  output [7:0] Y
);

  wire and_1_out, and_2_out, and_3_out, and_4_out, and_5_out, and_6_out, and_7_out, and_8_out, and_9_out,
       and_10_out, and_11_out, and_12_out, and_13_out, and_14_out, and_15_out, and_16_out, not_1_out,
       not_2_out;

  not not_1 (not_1_out, S);
  not not_2 (not_2_out, E);
  and and_1 (and_1_out, A0, S, not_2_out);
  and and_2 (and_2_out, A1, S, not_2_out);
  and and_3 (and_3_out, A2, S, not_2_out);
  and and_4 (and_4_out, A3, S, not_2_out);
  and and_5 (and_5_out, A4, S, not_2_out);
  and and_6 (and_6_out, A5, S, not_2_out);
  and and_7 (and_7_out, A6, S, not_2_out);
  and and_8 (and_8_out, A7, S, not_2_out);
  and and_9 (and_9_out, B0, not_1_out, not_2_out);
  and and_10 (and_10_out, B1, not_1_out, not_2_out);
  and and_11 (and_11_out, B2, not_1_out, not_2_out);
  and and_12 (and_12_out, B3, not_1_out, not_2_out);
  and and_13 (and_13_out, B4, not_1_out, not_2_out);
  and and_14 (and_14_out, B5, not_1_out, not_2_out);
  and and_15 (and_15_out, B6, not_1_out, not_2_out);
  and and_16 (and_16_out, B7, not_1_out, not_2_out);
  or or_1 (Y[0], and_1_out, and_9_out);
  or or_2 (Y[1], and_2_out, and_10_out);
  or or_3 (Y[2], and_3_out, and_11_out);
  or or_4 (Y[3], and_4_out, and_12_out);
  or or_5 (Y[4], and_5_out, and_13_out);
  or or_6 (Y[5], and_6_out, and_14_out);
  or or_7 (Y[6], and_7_out, and_15_out);
  or or_8 (Y[7], and_8_out, and_16_out);
endmodule
