// Logisim project Decoder4x16.circ as structural Verilog
module Dec3x8 (
  input  X,
  input  Y,
  input  Z,
  input  E,
  output D0,
  output D1,
  output D2,
  output D3,
  output D4,
  output D5,
  output D6,
  output D7
);

  wire not_1_out, not_2_out, not_3_out, not_4_out;

  not not_1 (not_1_out, X);
  not not_2 (not_2_out, Y);
  not not_3 (not_3_out, Z);
  not not_4 (not_4_out, E);
  and and_1 (D0, X, Y, Z, not_4_out);
  and and_2 (D1, not_1_out, Y, Z, not_4_out);
  and and_3 (D2, not_1_out, not_2_out, Z, not_4_out);
  and and_4 (D3, not_1_out, Y, not_3_out, not_4_out);
  and and_5 (D4, not_1_out, not_2_out, not_3_out, not_4_out);
  and and_6 (D5, X, not_2_out, not_3_out, not_4_out);
  and and_7 (D6, X, Y, not_3_out, not_4_out);
  and and_8 (D7, X, not_2_out, Z, not_4_out);
endmodule

module Dec4x16 (
  input  A3,
  input  A0,
  input  A1,
  input  A2,
  output D0,
  output D1,
  output D2,
  output D3,
  output D4,
  output D5,
  output D6,
  output D7,
  output D8,
  output D9,
  output D10,
  output D11,
  output D12,
  output D13,
  output D14,
  output D15
);

  wire not_1_out;

  not not_1 (not_1_out, A3);
  Dec3x8 dec3x8_1 (
    .X(A0), .Y(A1), .Z(A2), .E(A3), .D0(D0), .D1(D1), .D2(D2), .D3(D3), .D4(D4), .D5(D5), .D6(D6), .D7(D7));
  Dec3x8 dec3x8_2 (
    .X(A0), .Y(A1), .Z(A2), .E(not_1_out), .D0(D8), .D1(D9), .D2(D10), .D3(D11), .D4(D12), .D5(D13),
    .D6(D14), .D7(D15));
endmodule
